# Fritzing sketch manageCoil (saved by Fritzing 0.9.4)
breadboards: 1

parts:
  ESP1 = SWITCH SCIENCE ESPr Developer 32
  IC1 = IC, DIP package, 22 pins [chip_label=IC]
  VCC1 = Battery
  U1 = Vibration Motor- ROB-08449 [package=vibe-motor-10mm]
  U2 = Vibration Motor- ROB-08449 [package=vibe-motor-10mm]
  C1 = Electrolytic Capacitor [capacitance=1µF package="100 mil [THT, electrolytic]"]

nets:
  N1: ESP1.3v3, IC1.pin21
  N2: ESP1.io25, IC1.pin8
  N3: ESP1.io15, IC1.pin16
  N4: ESP1.io14, IC1.pin20
  N5: ESP1.io12, IC1.pin2
  N6: ESP1.io13, IC1.pin3
  N7: ESP1.gnd, IC1.pin5, IC1.pin6, IC1.pin17, IC1.pin18
  N8: ESP1.io27, IC1.pin7
  N9: IC1.pin1, IC1.pin11, VCC1.-, C1.-
  N10: IC1.pin4, U2.+
  N11: IC1.pin10, U1.+
  N12: IC1.pin12, IC1.pin22, VCC1.+, C1.+
  N13: IC1.pin13, U1.-
  N14: IC1.pin19, U2.-
